# Fritzing sketch v3_bela_esquemaInstrument_Crescente_WorkingSensors09_06 (saved by Fritzing 0.9.3b)
breadboards: 1

parts:
  Bela1 = Bela
  J1 = Basic Force Sensing Resistor (FSR) [package=THT]
  J2 = Basic Force Sensing Resistor (FSR) [package=THT]
  J3 = Basic Force Sensing Resistor (FSR) [package=THT]
  R1 = Resistor [tolerance=±5% resistance=10k package=THT]
  R2 = Resistor [tolerance=±5% resistance=10k package=THT]
  R3 = Resistor [tolerance=±5% resistance=10k package=THT]
  SP1 = SPEAKER [package=pcb_mount_speaker]
  Piezoelectric_Sensor1 = Piezoelectric Sensor
  R5 = Resistor [tolerance=±5% resistance=1M package=THT]
  Trill_Bar1 = Trill Bar
  Trill_Square1 = Trill Square
  J4 = Basic Force Sensing Resistor (FSR) [package=THT]
  R6 = Resistor [tolerance=±5% resistance=10k package=THT]
  R7 = Rotary Potentiometer (Large) [maximum_resistance=100kΩ package=THT]
  R8 = Rotary Potentiometer (Large) [maximum_resistance=100kΩ package=THT]
  S1 = Round Pushbutton

nets:
  GND: Bela1.P9_02_GND, R1.Pin_0, R2.Pin_0, R3.Pin_0, Piezoelectric_Sensor1.GND, Trill_Bar1.GND, Trill_Square1.GND, R6.Pin_0, R7.leg2, R8.leg2, S1.leg1
  VCC: Bela1.P9_04_3.3V, J1.pin_1, J2.pin_1, J3.pin_1, R5.Pin_0, Trill_Bar1.VCC, Trill_Square1.VCC, J4.pin_1, R7.leg1, R8.leg1
  N1: Bela1.P9_24_I2C1_SCL, Trill_Bar1.SCL, Trill_Square1.SCL
  N2: Bela1.P9_26_I2C1_SDA, Trill_Bar1.SDA, Trill_Square1.SDA
  N3: Bela1.P9_27, S1.leg0
  N4: Bela1.AIN_6, R7.wiper
  N5: Bela1.AIN_5, R8.wiper
  N6: Bela1.AIN_4, Piezoelectric_Sensor1.VCC, R5.Pin_1
  N7: Bela1.AIN_3, J3.pin_0, R3.Pin_1
  N8: Bela1.AIN_2, J2.pin_0, R2.Pin_1
  N9: Bela1.AIN_1, J1.pin_0, R1.Pin_1
  N10: Bela1.AIN_0, J4.pin_0, R6.Pin_1
  N11: Bela1.SPKR2_L, SP1.-
  N12: Bela1.SPKR2_R, SP1.+

custom parts:
  Bela: A Fritzing part for Bela
  Piezoelectric Sensor: Piezoelectric sensor.
  Trill Bar: A single-axis touch sensor with multi-touch sensing capabilities from Bela.io
  Trill Square: A 2-axis x/y touch sensor from Bela.io
